# Fritzing sketch wire (saved by Fritzing 1.0.5)
breadboards: 1

parts:
  Active_buzzer = Piezo Buzzer
  R1 = Resistor [tolerance=±5% power=0.25W resistance=1k package=THT]
  S1 = Pushbutton [package="[THT]"]
  Common_Anode = RGB LED (com. anode, rbg) [color="Red (633nm)" current=0.030A package="5 mm [THT]"]
  R4 = Resistor [tolerance=±5% power=0.25W resistance=220 package=THT]
  R5 = Resistor [tolerance=±5% power=0.25W resistance=220 package=THT]
  R6 = Resistor [tolerance=±5% power=0.25W resistance=220 package=THT]
  J1 = Basic Servo
  PIR1 = PIR sensor
  S8050_D331 = NPN-Transistor [package="TO92 [THT]"]
  YwRobot_Power_Supply1 = YwRobot Breadboard Power Supply [part_number=545043]
  Part2 = RFID-RC522-v3
  Part1 = Adafruit T-Cobbler Plus [part_number="Adafruit #1989 and #2028"]

nets:
  VCC: Active_buzzer.pin_1, J1.vcc, PIR1.VDD, YwRobot_Power_Supply1.VCC#5, YwRobot_Power_Supply1.VCC#6
  N1: Active_buzzer.pin_2, S8050_D331.C
  N2: R1.Pin_0, Part1.GPIO21
  N3: R1.Pin_1, S8050_D331.B
  N4: S1.Pin_1, S1.Pin_2, Part1.GPIO27
  GND: S1.Pin_3, S1.Pin_4, J1.gnd, PIR1.GND, S8050_D331.E, YwRobot_Power_Supply1.GND, Part2.GND, Part1.GND
  N5: Common_Anode.red_cathode, R4.Pin_1
  N6: Common_Anode.common_anode, YwRobot_Power_Supply1.VCC#9, YwRobot_Power_Supply1.VCC#10, Part2.3.3V
  N7: Common_Anode.blue_cathode, R5.Pin_1
  N8: Common_Anode.green_cathode, R6.Pin_1
  N9: R4.Pin_0, Part1.GPIO13
  N10: R5.Pin_0, Part1.GPIO19
  N11: R6.Pin_0, Part1.GPIO26
  N12: J1.pulse, Part1.GPIO18
  N13: PIR1.SIG, Part1.GPIO20
  N14: Part2.SDA, Part1.CE0
  N15: Part2.SCK, Part1.SCLK
  N16: Part2.MOSI, Part1.MOSI
  N17: Part2.MISO, Part1.MISO
  N18: Part2.RST, Part1.GPIO22

custom parts:
  Piezo Buzzer: Part from https://www.nutsvolts.com/magazine/article/november2012_SmileysWorkshop. Breadboard and icon images modified to be 0.3" in spacing and be more similar to the actual physical part.
  YwRobot Breadboard Power Supply: The YwRobot Breadboard Power Supply (MB-V2) has two power rails; they can be 5V or 3V3. Power to the module can be provided through the female USB socket or through the A10 (female) 2.1mm power jack.
  RFID-RC522-v3: A simple China made RFID-RC522 Reader (6x4 cm); do check the pin labels, as this is a MFRC522 based clone.
  Adafruit T-Cobbler Plus: The Raspberry Pi has landed on the Maker World like a 40-GPIO pinned, quad-USB ported, credit card sized bomb of DIY joy. And while you can use most of our great Model B accessories by hooking up our downgrade cable, its probably a good time to upgrade your set up and accessorize using all of the 40 pins. That's why we now carry the Assembled Adafruit Pi T-Cobbler Plus - Breakout + Cable for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
